// Logisim project Decod.circ as structural Verilog
module Decoder_subcircuit (
  input  En,
  input  A,
  input  B,
  output y0,
  output y1,
  output y2,
  output y3
);

  wire not_1_out, not_2_out;

  not not_1 (not_1_out, A);
  not not_2 (not_2_out, B);
  and and_1 (y0, not_1_out, En, not_2_out);
  and and_2 (y1, A, En, not_2_out);
  and and_3 (y2, not_1_out, En, B);
  and and_4 (y3, A, En, B);
endmodule
