// Logisim project PriorityEncoder.circ as structural Verilog: 2 circuits, main circuit main
module main (
);

  PE pe_1 ();  // open: A3, A2, A1, A0, Y1, Y0
  PE pe_2 ();  // open: A3, A2, A1, A0, Y1, Y0
  PE pe_3 ();  // open: A3, A2, A1, A0, Y1, Y0
  PE pe_4 ();  // open: A3, A2, A1, A0, Y1, Y0
  Hex_Digit_Display hex_digit_display_1 ();  // open: value, dp
endmodule

module PE (
  input  A3,
  input  A2,
  input  A1,
  input  A0,
  output Y1,
  output Y0
);

  wire and_1_out;

  and and_1 (and_1_out, ~A2, A1);  // AND_Gate
  or or_1 (Y1, A2, A3);
  or or_2 (Y0, A3, and_1_out);
endmodule
